# Fritzing sketch Potentiometers (saved by Fritzing 0.9.2b)
circuit board: 2.5cm x 3cm
breadboards: 1

parts:
  Pot_Backpack = male pin header, 9 pins [form="♂ (male)"]
  U1 = POT [package=pot_alpha_rv16af-20]
  U2 = POT [package=pot_alpha_rv16af-20]
  R1 = Resistor [tolerance=±5% resistance=220 package=THT]

nets:
  N1: Pot_Backpack.pin3, Pot_Backpack.pin4, U1.S, U2.S, R1.Pin_1
  N2: Pot_Backpack.pin8, U1.E, U2.A
  N3: Pot_Backpack.pin9, U1.A, U2.E, R1.Pin_0

notes:
  0
  1
  2
  3
  4
  3v3
  GND
  tx
  rx
