# Fritzing sketch Temperature (saved by Fritzing 0.9.2b)
circuit board: 2.5cm x 2cm
breadboards: 1

parts:
  Temp_Backpack = male pin header, 9 pins [form="♂ (male)"]
  R1 = Resistor [tolerance=±5% resistance=220 package=THT]
  T1 = LM35 Temperature Sensor [package="TO92 [THT]"]

nets:
  N1: Temp_Backpack.pin3, R1.Pin_1, T1.Vout
  N2: Temp_Backpack.pin8, T1.+Vs
  N3: Temp_Backpack.pin9, R1.Pin_0, T1.GND

notes:
  0
  1
  2
  3
  4
  3v3
  GND
  tx
  rx
