# Fritzing sketch SparkBot_PCB_Main-3.1 (saved by Fritzing 0.9.2b)
circuit board: 4.2cm x 5cm

parts:
  J1 = female pin header, 12 pins [form="♀ (female)"]
  J2 = female pin header, 12 pins [form="♀ (female)"]
  P1 = Piezo Speaker
  RI1 = Basic Servo
  LE1 = Basic Servo
  H1 = Basic Servo
  RGB = RGB LED (com. cathode, rbg) [package="5 mm [THT]"]
  B2 = female pin header, 2 pins [form="♀ (female)"]
  B1 = female pin header, 2 pins [form="♀ (female)"]
  R1 = Resistor [tolerance=±5% resistance=220 package=THT]
  I/O = female pin header, 9 pins [form="♀ (female)"]
  LDR = Photocell (LDR) [package=THT]
  MIC = Breakout Board for Electret Microphone
  RST = female pin header, 2 pins [form="♀ (female)"]

nets:
  VCC: J1.pin1, RI1.vcc, LE1.vcc, H1.vcc
  N1: J1.pin2, P1.pin1, R1.Pin_1, MIC.GND
  N2: J1.pin3, RGB.blue_anode
  N3: J1.pin4, P1.pin2
  N4: J1.pin5, RGB.green_anode
  N5: J1.pin6, I/O.pin7
  N6: J1.pin7, I/O.pin9
  N7: J1.pin8, I/O.pin8
  N8: J1.pin9, MIC.VCC
  N9: J1.pin10, I/O.pin5
  N10: J1.pin11, I/O.pin6
  N11: J1.pin12, J2.pin5, J2.pin6, B2.pin1, B1.pin1, R1.Pin_0, LDR.pin_0
  N12: J2.pin1, B2.pin2, B1.pin2, I/O.pin2, LDR.pin_1, MIC.AUD
  N13: J2.pin2, RST.pin1
  GND: J2.pin4, RI1.gnd, LE1.gnd, H1.gnd, RGB.common_cathode, I/O.pin1, RST.pin2
  N14: J2.pin7, I/O.pin4
  N15: J2.pin8, I/O.pin3
  N16: J2.pin9, RGB.red_anode
  N17: J2.pin10, H1.pulse
  N18: J2.pin11, LE1.pulse
  N19: J2.pin12, RI1.pulse

notes:
  GND
  4
  3
  2
  1
  0
  3v3
  G
  SparkBot
  GPIO / Backpack
  The IoT robotics kit for everyone.
  R
  L
  Photon
  |
  /\
  servos
  5
  6
  v3.0
