# Fritzing sketch SparkBot_PCB_Main-4.0 (saved by Fritzing 0.9.2b)
circuit board: 4.4cm x 10cm

parts:
  part = female pin header, 12 pins [form="♀ (female)"]
  part_2 = female pin header, 12 pins [form="♀ (female)"]
  P1 = Piezo Speaker
  RGB = RGB LED (com. cathode, rbg) [package="5 mm [THT]"]
  B2 = female pin header, 2 pins [form="♀ (female)"]
  B1 = female pin header, 2 pins [form="♀ (female)"]
  R1 = Resistor [tolerance=±5% resistance=220 package=THT]
  I/O = female pin header, 9 pins [form="♀ (female)"]
  LDR = Photocell (LDR) [package=THT]
  MIC = Breakout Board for Electret Microphone
  RST = female pin header, 2 pins [form="♀ (female)"]
  Nano = Arduino Nano (Rev3.0)
  part_3 = double row female pin header, 30 pins [form="♀ (female)"]
  part_4 = double row female pin header, 30 pins [form="♀ (female)"]
  RI1 = Basic Servo
  LE1 = Basic Servo
  H1 = Basic Servo
  R = female pin header, 4 pins [form="♀ (female)"]
  B = female pin header, 4 pins [form="♀ (female)"]
  G = female pin header, 4 pins [form="♀ (female)"]

nets:
  N1: part.pin2, R1.Pin_1, MIC.GND
  N2: part.pin3, Nano.D0/RX, part_4.pin2, part_4.pin29
  N3: part.pin4, Nano.D1/TX, part_4.pin1, part_4.pin30
  N4: part.pin5, RGB.green_anode
  N5: part.pin6, I/O.pin7
  N6: part.pin7, I/O.pin8
  N7: part.pin8, I/O.pin9
  N8: part.pin9, MIC.VCC
  N9: part.pin10, I/O.pin5
  N10: part.pin11, I/O.pin6
  N11: part.pin12, part_2.pin5, part_2.pin6, B2.pin1, B1.pin1, R1.Pin_0, LDR.pin_0
  N12: part_2.pin1, B2.pin2, B1.pin2, I/O.pin2, LDR.pin_1, MIC.AUD
  N13: part_2.pin2, RST.pin1
  N14: part_2.pin4, P1.pin1, RGB.common_cathode, I/O.pin1, RST.pin2
  N15: part_2.pin7, I/O.pin4
  N16: part_2.pin8, I/O.pin3
  N17: part_2.pin9, RGB.red_anode
  N18: part_2.pin10, RGB.blue_anode
  N19: part_2.pin12, P1.pin2
  N20: Nano.RESET, part_3.pin3, part_3.pin28, part_4.pin3, part_4.pin28
  GND: Nano.GND, part_3.pin2, part_3.pin29, part_4.pin4, part_4.pin27, RI1.gnd, LE1.gnd, H1.gnd, R.pin3, B.pin3, G.pin3
  N21: Nano.D2, part_4.pin5, part_4.pin26
  N22: Nano.D3, part_4.pin6, part_4.pin25, R.pin1, B.pin1, G.pin1
  N23: Nano.D4, part_4.pin7, part_4.pin24
  N24: Nano.D5, part_4.pin8, part_4.pin23, R.pin2, B.pin2, G.pin2
  N25: Nano.D6, part_4.pin9, part_4.pin22, R.pin4, B.pin4, G.pin4
  N26: Nano.D7, part_4.pin10, part_4.pin21
  N27: Nano.D8, part_4.pin11, part_4.pin20
  N28: Nano.D9, part_4.pin12, part_4.pin19, H1.pulse
  N29: Nano.D10, part_4.pin13, part_4.pin18, LE1.pulse
  N30: Nano.D11/MOSI, part_4.pin14, part_4.pin17, RI1.pulse
  N31: Nano.D12/MISO, part_4.pin15, part_4.pin16
  N32: Nano.VIN, part_3.pin1, part_3.pin30
  VCC: Nano.5V, part_3.pin4, part_3.pin27, RI1.vcc, LE1.vcc, H1.vcc
  N33: Nano.A7, part_3.pin5, part_3.pin26
  N34: Nano.A6, part_3.pin6, part_3.pin25
  N35: Nano.A5, part_3.pin7, part_3.pin24
  N36: Nano.A4, part_3.pin8, part_3.pin23
  N37: Nano.A3, part_3.pin9, part_3.pin22
  N38: Nano.A2, part_3.pin10, part_3.pin21
  N39: Nano.A1, part_3.pin11, part_3.pin20
  N40: Nano.A0, part_3.pin12, part_3.pin19
  N41: Nano.AREF, part_3.pin13, part_3.pin18
  N42: Nano.3V3, part_3.pin14, part_3.pin17
  N43: Nano.D13/SCK, part_3.pin15, part_3.pin16

notes:
  GND
  4
  3
  2
  1
  0
  3v3
  G
  SparkBot
  GPIO
  The IoT robotics kit for everyone.
  R
  L
  Photon
  |
  /\
  servos
  5
  6
  v4.0
  tx
  rx
  VIN
  5V
  3V3
  ANALOG
  A0
  7
  RST
