# Fritzing sketch SparkBot_PCB_Others (saved by Fritzing 0.9.2b)
circuit board: 1.5cm x 2cm
circuit board: 1cm x 1cm
circuit board: 1.5cm x 2cm
circuit board: 1.2cm x 2cm

parts:
  LED2 = RGB LED (com. cathode, rgb) [package="5 mm [THT]"]
  J4 = female pin header, 4 pins [form="♀ (female)"]
  LED3 = RGB LED (com. cathode, rgb) [package="5 mm [THT]"]
  J5 = female pin header, 4 pins [form="♀ (female)"]
  LED4 = RGB LED (com. cathode, rgb) [package="5 mm [THT]"]
  J6 = female pin header, 2 pins [form="♀ (female)"]
  S1 = Momentary Switch [package=tactile-pth]
  LED5 = RGB LED (com. cathode, rgb) [package="5 mm [THT]"]
  J7 = female pin header, 4 pins [form="♀ (female)"]
  J8 = female pin header, 2 pins [form="♀ (female)"]
  S2 = Momentary Switch [package=tactile-pth]
  R1 = Photocell (LDR) [package=THT]
  J9 = female pin header, 2 pins [form="♀ (female)"]

nets:
  N1: LED2.red_anode, J4.pin4
  N2: LED2.common_cathode, J4.pin3
  N3: LED2.green_anode, J4.pin2
  N4: LED2.blue_anode, J4.pin1
  N5: LED3.red_anode, J5.pin4, LED4.red_anode
  N6: LED3.common_cathode, J5.pin3, LED4.common_cathode
  N7: LED3.green_anode, J5.pin2, LED4.green_anode
  N8: LED3.blue_anode, J5.pin1, LED4.blue_anode
  N9: J6.pin1, S1.1
  N10: J6.pin2, S1.3
  N11: LED5.red_anode, J7.pin4
  N12: LED5.common_cathode, J7.pin3
  N13: LED5.green_anode, J7.pin2
  N14: LED5.blue_anode, J7.pin1
  N15: J8.pin1, S2.1
  N16: J8.pin2, S2.3
  N17: R1.pin_0, J9.pin1
  N18: R1.pin_1, J9.pin2
