# Fritzing sketch SparkBot-main (saved by Fritzing 0.9.1b)
circuit board: 3cm x 1.5cm
circuit board: 5cm x 3.5cm
circuit board: 1.5cm x 1.5cm
circuit board: 1.5cm x 1.5cm
circuit board: 1.5cm x 1.5cm
circuit board: 3cm x 1.5cm
circuit board: 1.3002cm x 3.07314cm
perfboards: 8

parts:
  LED1 = RGB LED (com. cathode, rbg) [package="5 mm [THT]"]
  LED2 = RGB LED (com. cathode, rbg) [package="5 mm [THT]"]
  LED4 = RGB LED (com. cathode, rbg) [package="5 mm [THT]"]
  LED3 = RGB LED (com. cathode, rbg) [package="5 mm [THT]"]
  J5 = female pin header, 12 pins [form="♀ (female)"]
  J4 = female pin header, 12 pins [form="♀ (female)"]
  J10 = Basic Servo
  J11 = Basic Servo
  J12 = Basic Servo
  J13 = Piezo Speaker
  S1 = Momentary Switch [package=ksa_sealed_tac_switch]
  S2 = Momentary Switch [package=ksa_sealed_tac_switch]
  R1 = Resistor [package="2512 [SMD]"]
  R2 = Resistor [package="2512 [SMD]"]
  U1 = TEMPERATURE-SENSOR [package=to-92]
  J14 = female pin header, 5 pins [form="♀ (female)"]
  J15 = female pin header, 3 pins [form="♀ (female)"]
  J16 = female pin header, 3 pins [form="♀ (female)"]
  J17 = female pin header, 4 pins [form="♀ (female)"]
  J18 = female pin header, 4 pins [form="♀ (female)"]
  J19 = female pin header, 4 pins [form="♀ (female)"]
  J20 = female pin header, 4 pins [form="♀ (female)"]
  J22 = female pin header, 5 pins [form="♀ (female)"]
  J23 = female pin header, 4 pins [form="♀ (female)"]
  Part1 = Spark Core (v1.0)

nets:
  N1: LED1.red_anode, LED2.red_anode, J17.pin1
  N2: LED1.common_cathode, LED2.common_cathode, J17.pin2
  N3: LED1.blue_anode, LED2.blue_anode, J17.pin3
  N4: LED1.green_anode, LED2.green_anode, J17.pin4
  N5: LED4.red_anode, J18.pin1
  N6: LED4.common_cathode, J18.pin2
  N7: LED4.blue_anode, J18.pin3
  N8: LED4.green_anode, J18.pin4
  N9: LED3.red_anode, J19.pin1
  N10: LED3.common_cathode, J19.pin2
  N11: LED3.blue_anode, J19.pin3
  N12: LED3.green_anode, J19.pin4
  N13: J5.pin1, J10.pulse, Part1.D0
  N14: J5.pin2, J11.pulse, Part1.D1
  N15: J5.pin3, J12.pulse, Part1.D2
  N16: J5.pin4, U1.ADJ, Part1.D3
  N17: J5.pin5, J23.pin1, Part1.D4
  N18: J5.pin6, J23.pin2, Part1.D5
  N19: J5.pin7, J23.pin4, Part1.D6
  N20: J5.pin8, Part1.D7
  GND: J5.pin9, J4.pin11, J4.pin12, J10.gnd, J11.gnd, J12.gnd, J13.pin1, U1.GND, J20.pin2, J23.pin3, Part1.GND, Part1.VIN
  N21: J5.pin10, Part1.3V3*
  N22: J5.pin11, Part1.RST
  VCC: J5.pin12, J10.vcc, J11.vcc, J12.vcc, U1.VCC, J20.pin3, Part1.3V3
  N23: J4.pin1, J13.pin2, Part1.A0
  N24: J4.pin2, J20.pin1, Part1.A1
  N25: J4.pin3, Part1.A2
  N26: J4.pin4, Part1.A3
  N27: J4.pin5, Part1.A4
  N28: J4.pin6, Part1.A5
  N29: J4.pin7, Part1.A6
  N30: J4.pin8, Part1.A7
  N31: J4.pin9, Part1.TX
  N32: J4.pin10, Part1.RX
  N33: S1.2, R1.Pin_1, J16.pin3
  N34: S1.4, J16.pin1
  N35: S2.2, R2.Pin_1, J15.pin3
  N36: S2.4, J15.pin1
  N37: R1.Pin_0, J16.pin2
  N38: R2.Pin_0, J15.pin2
  N39: J14.pin1, J22.pin1
  N40: J14.pin2, J14.pin3, J22.pin2, J22.pin3
  N41: J14.pin4, J22.pin4
  N42: J14.pin5, J22.pin5
